// Logisim project calc.circ as structural Verilog: 1 circuit, main circuit main
module main (
  input  in_1,
  input  in_2,
  input  in_3,
  input  in_4,
  input  in_5,
  input  \bit ,
  input  \reg ,
  input  in_8,
  input  DSA,
  input  DSB,
  input  in_11,
  input  nMR,
  input  in_13,
  input  CP,
  input  A,
  input  B,
  input  C,
  input  in_18
);

  wire a1_out, a2_out, a3_out, a4_out, a5_out, and_1_out, and_2_out, and_3_out, and_4_out, and_5_out,
       and_6_out, and_7_out, and_8_out, and_9_out, and_10_out, and_11_out, and_12_out, and_13_out,
       and_14_out, and_15_out, and_16_out, and_17_out, and_18_out, and_19_out, and_20_out, and_21_out,
       and_22_out, and_23_out, and_24_out, and_25_out, and_26_out, and_27_out, and_28_out, and_29_out,
       and_30_out, and_31_out, and_32_out, and_33_out, and_34_out, and_35_out, and_36_out, and_37_out,
       and_38_out, and_39_out, and_40_out, and_41_out, and_42_out, and_43_out, and_44_out, and_45_out,
       and_46_out, and_47_out, and_48_out, and_49_out, and_50_out, and_51_out, and_52_out, and_53_out,
       and_54_out, and_55_out, and_56_out, and_57_out, and_58_out, and_59_out, and_60_out, and_61_out,
       and_62_out, and_63_out, and_64_out, and_65_out, and_66_out, and_67_out, and_68_out, and_69_out,
       and_70_out, and_71_out, and_72_out, and_73_out, and_74_out, and_75_out, and_76_out, and_77_out,
       and_78_out, and_79_out, and_80_out, and_81_out, and_82_out, and_83_out, and_84_out, and_85_out,
       and_86_out, and_87_out, and_88_out, and_89_out, and_90_out, and_91_out, and_92_out, and_93_out,
       and_94_out, and_95_out, and_96_out, and_97_out, and_98_out, and_99_out, buffer_1_out, buffer_2_out,
       buffer_3_out, buffer_4_out, buffer_5_out, buffer_6_out, buffer_7_out, buffer_8_out, d_ff_1_q,
       d_ff_1_qn, d_ff_2_qn, d_ff_3_qn, d_ff_4_qn, d_ff_5_qn, d_ff_6_qn, d_ff_7_qn, d_ff_8_q, d_ff_9_qn,
       d_ff_10_q, d_ff_11_qn, d_ff_12_q, d_ff_13_q, d_ff_14_q, d_ff_15_q, d_ff_16_q, d_ff_17_q, n7485_1_pin1,
       n7485_1_pin2, n7485_1_pin3, n7485_1_pin4, n7485_1_pin5, n7485_1_pin6, n7485_1_pin7, n7485_1_pin9,
       n7485_1_pin10, n7485_1_pin11, n7485_1_pin12, n7485_1_pin13, n7485_1_pin14, n7485_1_pin15,
       n7485_2_pin1, n7485_2_pin9, n7485_2_pin11, n7485_2_pin14, n74377_1_pin2, n74377_1_pin3, n74377_1_pin4,
       n74377_1_pin5, n74377_1_pin6, n74377_1_pin7, n74377_1_pin8, n74377_1_pin9, n74377_1_pin11,
       n74377_1_pin12, n74377_1_pin13, n74377_1_pin14, n74377_1_pin15, n74377_1_pin16, n74377_1_pin17,
       n74377_1_pin18, n74377_1_pin19, n74377_2_pin2, n74377_2_pin5, n74377_2_pin6, n74377_2_pin9,
       n74377_2_pin12, n74377_2_pin15, n74377_2_pin16, n74377_2_pin19, n74377_3_pin2, n74377_3_pin5,
       n74377_3_pin6, n74377_3_pin9, n74377_3_pin12, n74377_3_pin15, n74377_3_pin16, n74377_3_pin19,
       n74377_4_pin2, n74377_4_pin5, n74377_4_pin6, n74377_4_pin9, n74377_4_pin12, n74377_4_pin15,
       n74377_4_pin16, n74377_4_pin19, n74377_5_pin1, n74377_5_pin2, n74377_5_pin3, n74377_5_pin4,
       n74377_5_pin5, n74377_5_pin6, n74377_5_pin7, n74377_5_pin8, n74377_5_pin9, n74377_5_pin12,
       n74377_5_pin13, n74377_5_pin14, n74377_5_pin15, n74377_5_pin16, n74377_5_pin17, n74377_5_pin18,
       n74377_5_pin19, n74377_6_pin2, n74377_6_pin5, n74377_6_pin6, n74377_6_pin9, n74377_6_pin12,
       n74377_6_pin15, n74377_6_pin16, n74377_6_pin19, n74377_7_pin19, n74377_8_pin1, n74377_8_pin2,
       n74377_8_pin3, n74377_8_pin4, n74377_8_pin5, n74377_8_pin6, n74377_8_pin7, n74377_8_pin8,
       n74377_9_pin12, n74377_9_pin15, n74377_9_pin16, n74377_9_pin19, nand_1_out, nand_2_out, nand_3_out,
       nand_4_out, nand_5_out, nand_6_out, nand_7_out, nand_8_out, nand_9_out, nor_1_out, nor_2_out,
       not_1_out, not_2_out, not_3_out, not_4_out, not_5_out, not_6_out, not_7_out, not_8_out, not_9_out,
       not_10_out, not_11_out, not_12_out, not_13_out, not_14_out, not_15_out, not_16_out, not_17_out,
       not_18_out, not_19_out, not_20_out, not_21_out, not_22_out, not_23_out, not_24_out, not_25_out,
       not_26_out, not_27_out, not_28_out, not_29_out, not_30_out, not_31_out, not_32_out, not_34_out,
       not_35_out, not_36_out, not_37_out, not_38_out, not_39_out, not_40_out, not_41_out, not_42_out,
       not_43_out, not_44_out, not_45_out, not_46_out, not_47_out, not_48_out, not_49_out, not_50_out,
       not_51_out, not_52_out, not_53_out, not_54_out, not_55_out, not_56_out, not_57_out, not_58_out,
       not_59_out, not_60_out, not_61_out, not_62_out, not_63_out, not_64_out, not_65_out, not_66_out,
       not_67_out, not_68_out, not_69_out, not_70_out, or_1_out, or_2_out, or_3_out, or_4_out, or_5_out,
       or_6_out, or_7_out, or_8_out, or_9_out, or_10_out, or_11_out, or_12_out, or_13_out, or_14_out,
       or_15_out, or_16_out, or_17_out, or_18_out, or_19_out, or_21_out, or_22_out, or_23_out, or_24_out,
       or_25_out, or_26_out, or_27_out, or_28_out, or_29_out, or_30_out, or_31_out, or_32_out, or_33_out,
       or_34_out, or_35_out, or_36_out, or_37_out, or_38_out, or_39_out, or_40_out, or_41_out, or_42_out,
       or_43_out, or_44_out, or_45_out, or_46_out, or_47_out, or_48_out, or_49_out, or_50_out, or_51_out,
       or_52_out, or_53_out, or_54_out, or_55_out, or_56_out, or_57_out, or_58_out, s1_out, s2_out, s3_out,
       s4_out, xnor_1_out, xnor_2_out, xnor_3_out, xnor_4_out, xnor_5_out, xnor_6_out, xnor_7_out,
       xnor_8_out, xor_1_out, xor_2_out, xor_3_out, xor_4_out, xor_5_out, xor_6_out, xor_7_out, xor_8_out,
       xor_9_out, xor_10_out, xor_11_out, xor_12_out, xor_13_out, xor_14_out, xor_15_out, xor_16_out,
       xor_17_out, xor_18_out, xor_19_out, xor_20_out, xor_21_out, xor_22_out, xor_23_out, xor_24_out,
       xor_25_out, xor_26_out, xor_27_out, xor_28_out, xor_29_out, xor_30_out, xor_31_out, xor_32_out;
  wire [7:0] d_ff_2_q, rom_1_data, rom_2_data;

  not not_1 (not_1_out, rom_2_data[3]);
  or or_1 (or_1_out, rom_2_data[1], rom_2_data[2]);
  or or_2 (or_2_out, rom_2_data[0], or_3_out);
  or or_3 (or_3_out, rom_2_data[2], rom_2_data[3]);
  and and_1 (and_1_out, rom_2_data[0], rom_2_data[1]);
  or or_4 (or_4_out, rom_2_data[2], rom_2_data[3]);
  or or_5 (or_5_out, rom_2_data[1], rom_2_data[3]);
  and and_2 (and_2_out, rom_2_data[0], rom_2_data[2]);
  or or_6 (or_6_out, rom_2_data[1], rom_2_data[3]);
  and and_3 (and_3_out, rom_2_data[1], rom_2_data[2]);
  or or_7 (or_7_out, rom_2_data[0], rom_2_data[3]);
  not not_2 (not_2_out, or_7_out);
  and and_4 (and_4_out, rom_2_data[0], rom_2_data[1]);
  and and_5 (and_5_out, rom_2_data[2], not_1_out);
  or or_8 (or_8_out, rom_2_data[1], rom_2_data[2]);
  and and_6 (and_6_out, rom_2_data[0], rom_2_data[3]);
  or or_9 (or_9_out, rom_2_data[1], rom_2_data[2]);
  not not_3 (not_3_out, or_9_out);
  and and_7 (and_7_out, rom_2_data[1], rom_2_data[3]);
  or or_10 (or_10_out, rom_2_data[0], rom_2_data[2]);
  not not_4 (not_4_out, or_10_out);
  and and_8 (and_8_out, rom_2_data[0], rom_2_data[1]);
  not not_5 (not_5_out, rom_2_data[2]);
  and and_9 (and_9_out, not_5_out, rom_2_data[3]);
  and and_10 (and_10_out, rom_2_data[2], rom_2_data[3]);
  or or_11 (or_11_out, rom_2_data[0], rom_2_data[1]);
  not not_6 (not_6_out, or_11_out);
  or or_12 (or_12_out, or_1_out, rom_2_data[3]);
  not not_7 (not_7_out, or_12_out);
  not not_8 (not_8_out, or_2_out);
  not not_9 (not_9_out, or_4_out);
  or or_13 (or_13_out, rom_2_data[0], or_5_out);
  not not_10 (not_10_out, or_13_out);
  not not_11 (not_11_out, or_6_out);
  and and_11 (and_11_out, and_3_out, not_2_out);
  and and_12 (and_12_out, and_4_out, and_5_out);
  or or_14 (or_14_out, rom_2_data[0], or_8_out);
  not not_12 (not_12_out, or_14_out);
  and and_13 (and_13_out, and_6_out, not_3_out);
  and and_14 (and_14_out, and_7_out, not_4_out);
  and and_15 (and_15_out, and_8_out, and_9_out);
  and and_16 (and_16_out, and_10_out, not_6_out);
  and and_17 (and_17_out, rom_2_data[0], not_7_out);
  and and_18 (and_18_out, rom_2_data[1], not_8_out);
  and and_19 (and_19_out, and_1_out, not_9_out);
  and and_20 (and_20_out, rom_2_data[2], not_10_out);
  and and_21 (and_21_out, and_2_out, not_11_out);
  and and_22 (and_22_out, rom_2_data[3], not_12_out);
  or or_15 (or_15_out, rom_2_data[5], rom_2_data[6]);
  or or_16 (or_16_out, rom_2_data[6], rom_2_data[7]);
  or or_17 (or_17_out, rom_2_data[6], rom_2_data[7]);
  or or_18 (or_18_out, rom_2_data[5], rom_2_data[7]);
  and and_23 (and_23_out, rom_2_data[4], rom_2_data[6]);
  or or_19 (or_19_out, rom_2_data[5], rom_2_data[7]);
  and and_24 (and_24_out, rom_2_data[5], rom_2_data[6]);
  // OR_Gate or_20 has open pins: in0=rom_2_data[4], in1=rom_2_data[7], out=open
  // NOT_Gate not_13 has open pins: in=open, out=not_13_out
  and and_25 (and_25_out, rom_2_data[4], rom_2_data[5]);
  and and_26 (and_26_out, rom_2_data[6], not_14_out);
  not not_14 (not_14_out, rom_2_data[7]);
  or or_21 (or_21_out, rom_2_data[5], rom_2_data[6]);
  and and_27 (and_27_out, rom_2_data[4], rom_2_data[7]);
  or or_22 (or_22_out, rom_2_data[5], rom_2_data[6]);
  not not_15 (not_15_out, or_22_out);
  and and_28 (and_28_out, rom_2_data[5], rom_2_data[7]);
  or or_23 (or_23_out, rom_2_data[4], rom_2_data[6]);
  not not_16 (not_16_out, or_23_out);
  and and_29 (and_29_out, rom_2_data[4], rom_2_data[5]);
  not not_17 (not_17_out, rom_2_data[6]);
  and and_30 (and_30_out, rom_2_data[6], rom_2_data[7]);
  or or_24 (or_24_out, rom_2_data[4], rom_2_data[5]);
  not not_18 (not_18_out, or_24_out);
  or or_25 (or_25_out, or_15_out, rom_2_data[7]);
  not not_19 (not_19_out, or_25_out);
  or or_26 (or_26_out, rom_2_data[4], or_16_out);
  not not_20 (not_20_out, or_26_out);
  and and_31 (and_31_out, rom_2_data[4], rom_2_data[5]);
  not not_21 (not_21_out, or_17_out);
  or or_27 (or_27_out, rom_2_data[4], or_18_out);
  not not_22 (not_22_out, or_19_out);
  and and_32 (and_32_out, and_24_out, not_13_out);
  and and_33 (and_33_out, and_25_out, and_26_out);
  or or_28 (or_28_out, rom_2_data[4], or_21_out);
  not not_23 (not_23_out, or_28_out);
  and and_34 (and_34_out, and_27_out, not_15_out);
  and and_35 (and_35_out, and_28_out, not_16_out);
  and and_36 (and_36_out, not_17_out, rom_2_data[7]);
  and and_37 (and_37_out, and_30_out, not_18_out);
  and and_38 (and_38_out, rom_2_data[4], not_19_out);
  and and_39 (and_39_out, rom_2_data[5], not_20_out);
  and and_40 (and_40_out, and_31_out, not_21_out);
  not not_24 (not_24_out, or_27_out);
  and and_41 (and_41_out, and_23_out, not_22_out);
  and and_42 (and_42_out, rom_2_data[7], not_23_out);
  and and_43 (and_43_out, and_29_out, and_36_out);
  and and_44 (and_44_out, rom_2_data[6], not_24_out);
  D_Flip_Flop d_ff_1 (.D(d_ff_1_qn), .clk(n74377_1_pin11), .Q(d_ff_1_q), .Qn(d_ff_1_qn));  // open: preset, reset
  D_Flip_Flop d_ff_2 (.D(d_ff_2_qn), .clk(d_ff_1_q), .Q(d_ff_2_q[0]), .Qn(d_ff_2_qn), .reset(in_18));  // open: preset
  D_Flip_Flop d_ff_3 (.D(d_ff_3_qn), .clk(d_ff_2_qn), .Q(d_ff_2_q[1]), .Qn(d_ff_3_qn), .reset(in_18));  // open: preset
  D_Flip_Flop d_ff_4 (.D(d_ff_4_qn), .clk(d_ff_3_qn), .Q(d_ff_2_q[2]), .Qn(d_ff_4_qn), .reset(in_18));  // open: preset
  D_Flip_Flop d_ff_5 (.D(d_ff_5_qn), .clk(d_ff_4_qn), .Q(d_ff_2_q[3]), .Qn(d_ff_5_qn), .reset(in_18));  // open: preset
  not not_25 (not_25_out, and_20_out);
  D_Flip_Flop d_ff_6 (.D(d_ff_6_qn), .clk(d_ff_5_qn), .Q(d_ff_2_q[4]), .Qn(d_ff_6_qn), .reset(in_18));  // open: preset
  not not_26 (not_26_out, and_21_out);
  and and_45 (and_45_out, DSA, DSB);
  not not_27 (not_27_out, nMR);
  D_Flip_Flop d_ff_7 (.D(d_ff_7_qn), .clk(d_ff_6_qn), .Q(d_ff_2_q[5]), .Qn(d_ff_7_qn), .reset(in_18));  // open: preset
  _74377 #(.ShowInternalStructure("true")) u_74377_1 (
    .pin1(not_25_out), .pin2(n74377_1_pin2), .pin3(n74377_1_pin3), .pin4(n74377_1_pin4),
    .pin5(n74377_1_pin5), .pin6(n74377_1_pin6), .pin7(n74377_1_pin7), .pin8(n74377_1_pin8),
    .pin9(n74377_1_pin9), .pin19(n74377_1_pin19), .pin18(n74377_1_pin18), .pin17(n74377_1_pin17),
    .pin16(n74377_1_pin16), .pin15(n74377_1_pin15), .pin14(n74377_1_pin14), .pin13(n74377_1_pin13),
    .pin12(n74377_1_pin12), .pin11(n74377_1_pin11));
  not not_28 (not_28_out, and_17_out);
  D_Flip_Flop d_ff_8 (.D(and_45_out), .clk(CP), .Q(d_ff_8_q), .reset(not_27_out));  // open: Qn, preset
  D_Flip_Flop d_ff_9 (.D(d_ff_9_qn), .clk(d_ff_7_qn), .Q(d_ff_2_q[6]), .Qn(d_ff_9_qn), .reset(in_18));  // open: preset
  _74377 #(.ShowInternalStructure("true")) u_74377_2 (
    .pin1(not_26_out), .pin2(n74377_2_pin2), .pin3(n74377_1_pin3), .pin4(n74377_1_pin4),
    .pin5(n74377_2_pin5), .pin6(n74377_2_pin6), .pin7(n74377_1_pin7), .pin8(n74377_1_pin8),
    .pin9(n74377_2_pin9), .pin19(n74377_2_pin19), .pin18(n74377_1_pin18), .pin17(n74377_1_pin17),
    .pin16(n74377_2_pin16), .pin15(n74377_2_pin15), .pin14(n74377_1_pin14), .pin13(n74377_1_pin13),
    .pin12(n74377_2_pin12), .pin11(n74377_1_pin11));
  _74377 #(.ShowInternalStructure("true")) u_74377_3 (
    .pin1(not_28_out), .pin2(n74377_3_pin2), .pin3(n74377_1_pin3), .pin4(n74377_1_pin4),
    .pin5(n74377_3_pin5), .pin6(n74377_3_pin6), .pin7(n74377_1_pin7), .pin8(n74377_1_pin8),
    .pin9(n74377_3_pin9), .pin19(n74377_3_pin19), .pin18(n74377_1_pin18), .pin17(n74377_1_pin17),
    .pin16(n74377_3_pin16), .pin15(n74377_3_pin15), .pin14(n74377_1_pin14), .pin13(n74377_1_pin13),
    .pin12(n74377_3_pin12), .pin11(n74377_1_pin11));
  D_Flip_Flop d_ff_10 (.D(d_ff_8_q), .clk(CP), .Q(d_ff_10_q), .reset(not_27_out));  // open: Qn, preset
  buf buffer_1 (buffer_1_out, d_ff_8_q);
  buf buffer_2 (buffer_2_out, d_ff_10_q);
  D_Flip_Flop d_ff_11 (
    .D(d_ff_11_qn), .clk(d_ff_9_qn), .Q(d_ff_2_q[7]), .Qn(d_ff_11_qn), .reset(in_18));  // open: preset
  D_Flip_Flop d_ff_12 (.D(d_ff_10_q), .clk(CP), .Q(d_ff_12_q), .reset(not_27_out));  // open: Qn, preset
  assign n74377_1_pin18 = and_40_out ? n74377_2_pin19 : 1'bz;  // Controlled_Buffer controlled_buffer_1
  assign n74377_1_pin17 = and_40_out ? n74377_2_pin16 : 1'bz;  // Controlled_Buffer controlled_buffer_2
  assign n74377_1_pin14 = and_40_out ? n74377_2_pin15 : 1'bz;  // Controlled_Buffer controlled_buffer_3
  assign n74377_1_pin13 = and_40_out ? n74377_2_pin12 : 1'bz;  // Controlled_Buffer controlled_buffer_4
  assign n74377_1_pin8 = and_40_out ? n74377_2_pin9 : 1'bz;  // Controlled_Buffer controlled_buffer_5
  assign n74377_1_pin7 = and_40_out ? n74377_2_pin6 : 1'bz;  // Controlled_Buffer controlled_buffer_6
  assign n74377_1_pin4 = and_40_out ? n74377_2_pin5 : 1'bz;  // Controlled_Buffer controlled_buffer_7
  assign n74377_1_pin3 = and_40_out ? n74377_2_pin2 : 1'bz;  // Controlled_Buffer controlled_buffer_8
  assign n74377_1_pin18 = and_39_out ? n74377_1_pin19 : 1'bz;  // Controlled_Buffer controlled_buffer_9
  assign n74377_1_pin17 = and_39_out ? n74377_1_pin16 : 1'bz;  // Controlled_Buffer controlled_buffer_10
  assign n74377_1_pin14 = and_39_out ? n74377_1_pin15 : 1'bz;  // Controlled_Buffer controlled_buffer_11
  assign n74377_1_pin13 = and_39_out ? n74377_1_pin12 : 1'bz;  // Controlled_Buffer controlled_buffer_12
  assign n74377_1_pin8 = and_39_out ? n74377_1_pin9 : 1'bz;  // Controlled_Buffer controlled_buffer_13
  assign n74377_1_pin7 = and_39_out ? n74377_1_pin6 : 1'bz;  // Controlled_Buffer controlled_buffer_14
  assign n74377_1_pin4 = and_39_out ? n74377_1_pin5 : 1'bz;  // Controlled_Buffer controlled_buffer_15
  assign n74377_1_pin3 = and_39_out ? n74377_1_pin2 : 1'bz;  // Controlled_Buffer controlled_buffer_16
  assign n74377_1_pin18 = and_38_out ? n74377_3_pin19 : 1'bz;  // Controlled_Buffer controlled_buffer_17
  assign n74377_1_pin17 = and_38_out ? n74377_3_pin16 : 1'bz;  // Controlled_Buffer controlled_buffer_18
  assign n74377_1_pin14 = and_38_out ? n74377_3_pin15 : 1'bz;  // Controlled_Buffer controlled_buffer_19
  assign n74377_1_pin13 = and_38_out ? n74377_3_pin12 : 1'bz;  // Controlled_Buffer controlled_buffer_20
  assign n74377_1_pin8 = and_38_out ? n74377_3_pin9 : 1'bz;  // Controlled_Buffer controlled_buffer_21
  assign n74377_1_pin7 = and_38_out ? n74377_3_pin6 : 1'bz;  // Controlled_Buffer controlled_buffer_22
  assign n74377_1_pin4 = and_38_out ? n74377_3_pin5 : 1'bz;  // Controlled_Buffer controlled_buffer_23
  assign n74377_1_pin3 = and_38_out ? n74377_3_pin2 : 1'bz;  // Controlled_Buffer controlled_buffer_24
  D_Flip_Flop d_ff_13 (.D(d_ff_12_q), .clk(CP), .Q(d_ff_13_q), .reset(not_27_out));  // open: Qn, preset
  buf buffer_3 (buffer_3_out, d_ff_12_q);
  D_Flip_Flop d_ff_14 (.D(d_ff_13_q), .clk(CP), .Q(d_ff_14_q), .reset(not_27_out));  // open: Qn, preset
  buf buffer_4 (buffer_4_out, d_ff_13_q);
  Clock clock_1 (.out(n74377_1_pin11));
  D_Flip_Flop d_ff_15 (.D(d_ff_14_q), .clk(CP), .Q(d_ff_15_q), .reset(not_27_out));  // open: Qn, preset
  buf buffer_5 (buffer_5_out, d_ff_14_q);
  LED led_1 (.in(or_32_out));
  and and_46 (and_46_out, not_29_out, xor_1_out);
  not not_29 (not_29_out, or_38_out);
  not not_30 (not_30_out, and_19_out);
  not not_31 (not_31_out, and_18_out);
  buf buffer_6 (buffer_6_out, d_ff_15_q);
  assign n74377_1_pin3 = and_44_out ? n74377_5_pin2 : 1'bz;  // Controlled_Buffer controlled_buffer_25
  assign n74377_1_pin4 = and_44_out ? n74377_5_pin5 : 1'bz;  // Controlled_Buffer controlled_buffer_26
  assign n74377_1_pin7 = and_44_out ? n74377_5_pin6 : 1'bz;  // Controlled_Buffer controlled_buffer_27
  assign n74377_1_pin8 = and_44_out ? n74377_5_pin9 : 1'bz;  // Controlled_Buffer controlled_buffer_28
  assign n74377_1_pin13 = and_44_out ? n74377_5_pin12 : 1'bz;  // Controlled_Buffer controlled_buffer_29
  assign n74377_1_pin14 = and_44_out ? n74377_5_pin15 : 1'bz;  // Controlled_Buffer controlled_buffer_30
  assign n74377_1_pin17 = and_44_out ? n74377_5_pin16 : 1'bz;  // Controlled_Buffer controlled_buffer_31
  assign n74377_1_pin18 = and_44_out ? n74377_5_pin19 : 1'bz;  // Controlled_Buffer controlled_buffer_32
  or or_29 (or_29_out, and_46_out, and_47_out);
  and and_47 (and_47_out, or_38_out, xnor_1_out);
  xor xor_1 (xor_1_out, n74377_6_pin2, n74377_4_pin2);
  D_Flip_Flop d_ff_16 (.D(d_ff_15_q), .clk(CP), .Q(d_ff_16_q), .reset(not_27_out));  // open: Qn, preset
  ROM rom_1 (.addr(d_ff_2_q), .data(rom_1_data));
  not not_32 (not_32_out, or_31_out);
  or or_30 (or_30_out, and_42_out, and_12_out);
  and and_48 (and_48_out, n74377_4_pin2, xor_2_out);
  xnor xnor_1 (xnor_1_out, n74377_6_pin2, n74377_4_pin2);
  LED led_2 (.in(or_35_out));
  _74377 #(.ShowInternalStructure("true")) u_74377_4 (
    .pin1(not_31_out), .pin2(n74377_4_pin2), .pin3(n74377_1_pin3), .pin4(n74377_1_pin4),
    .pin5(n74377_4_pin5), .pin6(n74377_4_pin6), .pin7(n74377_1_pin7), .pin8(n74377_1_pin8),
    .pin9(n74377_4_pin9), .pin19(n74377_4_pin19), .pin18(n74377_1_pin18), .pin17(n74377_1_pin17),
    .pin16(n74377_4_pin16), .pin15(n74377_4_pin15), .pin14(n74377_1_pin14), .pin13(n74377_1_pin13),
    .pin12(n74377_4_pin12), .pin11(n74377_1_pin11));
  D_Flip_Flop d_ff_17 (.D(d_ff_16_q), .clk(CP), .Q(d_ff_17_q), .reset(not_27_out));  // open: Qn, preset
  buf buffer_7 (buffer_7_out, d_ff_16_q);
  or or_31 (or_31_out, or_33_out, or_34_out);
  _74377 #(.ShowInternalStructure("true")) u_74377_5 (
    .pin1(n74377_5_pin1), .pin2(n74377_5_pin2), .pin3(n74377_5_pin3), .pin4(n74377_5_pin4),
    .pin5(n74377_5_pin5), .pin6(n74377_5_pin6), .pin7(n74377_5_pin7), .pin8(n74377_5_pin8),
    .pin9(n74377_5_pin9), .pin19(n74377_5_pin19), .pin18(n74377_5_pin18), .pin17(n74377_5_pin17),
    .pin16(n74377_5_pin16), .pin15(n74377_5_pin15), .pin14(n74377_5_pin14), .pin13(n74377_5_pin13),
    .pin12(n74377_5_pin12), .pin11(n74377_1_pin11));
  not not_33 (n74377_5_pin1, or_30_out);
  or or_32 (or_32_out, and_48_out, and_49_out);
  and and_49 (and_49_out, n74377_6_pin2, or_38_out);
  xor xor_2 (xor_2_out, n74377_6_pin2, or_38_out);
  xor xor_3 (xor_3_out, xor_4_out, or_37_out);
  xor xor_4 (xor_4_out, n74377_4_pin2, n74377_6_pin2);
  buf buffer_8 (buffer_8_out, d_ff_17_q);
  or or_33 (or_33_out, rom_2_data[4], rom_2_data[5]);
  or or_34 (or_34_out, rom_2_data[6], rom_2_data[7]);
  and and_50 (and_50_out, not_34_out, xor_5_out);
  not not_34 (not_34_out, or_41_out);
  or or_35 (or_35_out, and_51_out, and_52_out);
  and and_51 (and_51_out, or_37_out, not_35_out);
  not not_35 (not_35_out, xor_4_out);
  and and_52 (and_52_out, n74377_6_pin2, not_36_out);
  not not_36 (not_36_out, n74377_4_pin2);
  or or_36 (or_36_out, and_50_out, and_53_out);
  and and_53 (and_53_out, or_41_out, xnor_2_out);
  xor xor_5 (xor_5_out, n74377_6_pin5, n74377_4_pin5);
  xor xor_6 (xor_6_out, xor_7_out, or_40_out);
  xor xor_7 (xor_7_out, n74377_4_pin5, n74377_6_pin5);
  assign n74377_1_pin3 = not_32_out ? rom_1_data[7] : 1'bz;  // Controlled_Buffer controlled_buffer_33
  assign n74377_1_pin4 = not_32_out ? rom_1_data[6] : 1'bz;  // Controlled_Buffer controlled_buffer_34
  assign n74377_1_pin7 = not_32_out ? rom_1_data[5] : 1'bz;  // Controlled_Buffer controlled_buffer_35
  assign n74377_5_pin3 = not_39_out ? or_29_out : 1'bz;  // Controlled_Buffer controlled_buffer_36
  assign n74377_5_pin4 = not_39_out ? or_36_out : 1'bz;  // Controlled_Buffer controlled_buffer_37
  and and_54 (and_54_out, n74377_4_pin5, xor_8_out);
  xnor xnor_2 (xnor_2_out, n74377_6_pin5, n74377_4_pin5);
  or or_37 (or_37_out, and_55_out, and_56_out);
  and and_55 (and_55_out, or_40_out, not_37_out);
  not not_37 (not_37_out, xor_7_out);
  and and_56 (and_56_out, n74377_6_pin5, not_38_out);
  not not_38 (not_38_out, n74377_4_pin5);
  _74377 #(.ShowInternalStructure("true")) u_74377_6 (
    .pin1(not_30_out), .pin2(n74377_6_pin2), .pin3(n74377_1_pin3), .pin4(n74377_1_pin4),
    .pin5(n74377_6_pin5), .pin6(n74377_6_pin6), .pin7(n74377_1_pin7), .pin8(n74377_1_pin8),
    .pin9(n74377_6_pin9), .pin19(n74377_6_pin19), .pin18(n74377_1_pin18), .pin17(n74377_1_pin17),
    .pin16(n74377_6_pin16), .pin15(n74377_6_pin15), .pin14(n74377_1_pin14), .pin13(n74377_1_pin13),
    .pin12(n74377_6_pin12), .pin11(n74377_1_pin11));
  assign n74377_1_pin8 = not_32_out ? rom_1_data[4] : 1'bz;  // Controlled_Buffer controlled_buffer_38
  assign n74377_1_pin13 = not_32_out ? rom_1_data[3] : 1'bz;  // Controlled_Buffer controlled_buffer_39
  assign n74377_1_pin14 = not_32_out ? rom_1_data[2] : 1'bz;  // Controlled_Buffer controlled_buffer_40
  assign n74377_1_pin17 = not_32_out ? rom_1_data[1] : 1'bz;  // Controlled_Buffer controlled_buffer_41
  assign n74377_5_pin7 = not_39_out ? or_39_out : 1'bz;  // Controlled_Buffer controlled_buffer_42
  assign n74377_5_pin8 = not_39_out ? or_43_out : 1'bz;  // Controlled_Buffer controlled_buffer_43
  assign n74377_5_pin13 = not_39_out ? or_49_out : 1'bz;  // Controlled_Buffer controlled_buffer_44
  assign n74377_5_pin14 = not_39_out ? or_52_out : 1'bz;  // Controlled_Buffer controlled_buffer_45
  or or_38 (or_38_out, and_54_out, and_57_out);
  and and_57 (and_57_out, n74377_6_pin5, or_41_out);
  xor xor_8 (xor_8_out, n74377_6_pin5, or_41_out);
  LED led_3 (.in(n74377_7_pin19));
  _74377 #(.ShowInternalStructure("true")) u_74377_7 (
    .pin1(in_8), .pin19(n74377_7_pin19), .pin18(in_3), .pin11(in_4));  // open: pin2, pin3, pin4, pin5, pin6, pin7, pin8, pin9, pin17, pin16, pin15, pin14, pin13, pin12
  ROM rom_2 (.addr(d_ff_2_q), .data(rom_2_data));
  assign n74377_1_pin18 = not_32_out ? rom_1_data[0] : 1'bz;  // Controlled_Buffer controlled_buffer_46
  not not_39 (not_39_out, and_42_out);
  assign n74377_5_pin17 = not_39_out ? or_55_out : 1'bz;  // Controlled_Buffer controlled_buffer_47
  assign n74377_5_pin18 = not_39_out ? or_57_out : 1'bz;  // Controlled_Buffer controlled_buffer_48
  and and_58 (and_58_out, not_40_out, xor_11_out);
  not not_40 (not_40_out, or_46_out);
  xor xor_9 (xor_9_out, xor_10_out, or_42_out);
  xor xor_10 (xor_10_out, n74377_4_pin6, n74377_6_pin6);
  and and_59 (and_59_out, n74377_6_pin6, not_42_out);
  or or_39 (or_39_out, and_58_out, and_60_out);
  and and_60 (and_60_out, or_46_out, xnor_3_out);
  xor xor_11 (xor_11_out, n74377_6_pin6, n74377_4_pin6);
  or or_40 (or_40_out, and_61_out, and_59_out);
  and and_61 (and_61_out, or_42_out, not_41_out);
  not not_41 (not_41_out, xor_10_out);
  not not_42 (not_42_out, n74377_4_pin6);
  and and_62 (and_62_out, n74377_4_pin6, xor_14_out);
  xnor xnor_3 (xnor_3_out, n74377_6_pin6, n74377_4_pin6);
  xor xor_12 (xor_12_out, xor_13_out, or_44_out);
  xor xor_13 (xor_13_out, n74377_4_pin9, n74377_6_pin9);
  or or_41 (or_41_out, and_62_out, and_63_out);
  and and_63 (and_63_out, n74377_6_pin6, or_46_out);
  xor xor_14 (xor_14_out, n74377_6_pin6, or_46_out);
  or or_42 (or_42_out, and_64_out, and_65_out);
  and and_64 (and_64_out, or_44_out, not_43_out);
  not not_43 (not_43_out, xor_13_out);
  and and_65 (and_65_out, n74377_6_pin9, not_44_out);
  not not_44 (not_44_out, n74377_4_pin9);
  assign n74377_1_pin3 = or_45_out ? 1'b0 : 1'bz;  // Controlled_Buffer controlled_buffer_49
  not not_45 (not_45_out, and_11_out);
  and and_66 (and_66_out, not_46_out, xor_16_out);
  not not_46 (not_46_out, or_51_out);
  xor xor_15 (xor_15_out, n74377_4_pin12, n74377_6_pin12);
  assign n74377_1_pin4 = or_45_out ? 1'b0 : 1'bz;  // Controlled_Buffer controlled_buffer_50
  assign n74377_1_pin7 = or_45_out ? 1'b0 : 1'bz;  // Controlled_Buffer controlled_buffer_51
  assign n74377_1_pin8 = or_45_out ? 1'b0 : 1'bz;  // Controlled_Buffer controlled_buffer_52
  assign n74377_1_pin13 = or_45_out ? 1'b0 : 1'bz;  // Controlled_Buffer controlled_buffer_53
  or or_43 (or_43_out, and_66_out, and_67_out);
  and and_67 (and_67_out, or_51_out, xnor_4_out);
  xor xor_16 (xor_16_out, n74377_6_pin9, n74377_4_pin9);
  xor xor_17 (xor_17_out, xor_15_out, or_48_out);
  and and_68 (and_68_out, or_48_out, not_48_out);
  and and_69 (and_69_out, n74377_6_pin12, not_47_out);
  not not_47 (not_47_out, n74377_4_pin12);
  assign n74377_1_pin14 = or_45_out ? 1'b0 : 1'bz;  // Controlled_Buffer controlled_buffer_54
  assign n74377_1_pin17 = or_45_out ? 1'b0 : 1'bz;  // Controlled_Buffer controlled_buffer_55
  and and_70 (and_70_out, n74377_4_pin9, xor_18_out);
  xnor xnor_4 (xnor_4_out, n74377_6_pin9, n74377_4_pin9);
  or or_44 (or_44_out, and_68_out, and_69_out);
  not not_48 (not_48_out, xor_15_out);
  or or_45 (or_45_out, and_33_out, or_47_out);
  _74377 #(.ShowInternalStructure("true")) u_74377_8 (
    .pin1(n74377_8_pin1), .pin2(n74377_8_pin2), .pin3(n74377_8_pin3), .pin4(n74377_8_pin4),
    .pin5(n74377_8_pin5), .pin6(n74377_8_pin6), .pin7(n74377_8_pin7), .pin8(n74377_8_pin8),
    .pin11(n74377_1_pin11));  // open: pin9, pin19, pin18, pin17, pin16, pin15, pin14, pin13, pin12
  _7485 #(.ShowInternalStructure("true")) u_7485_1 (
    .pin1(n7485_1_pin1), .pin2(n7485_1_pin2), .pin3(n7485_1_pin3), .pin4(n7485_1_pin4), .pin5(n7485_1_pin5),
    .pin6(n7485_1_pin6), .pin7(n7485_1_pin7), .pin15(n7485_1_pin15), .pin14(n7485_1_pin14),
    .pin13(n7485_1_pin13), .pin12(n7485_1_pin12), .pin11(n7485_1_pin11), .pin10(n7485_1_pin10),
    .pin9(n7485_1_pin9));
  or or_46 (or_46_out, and_70_out, and_71_out);
  and and_71 (and_71_out, n74377_6_pin9, or_51_out);
  xor xor_18 (xor_18_out, n74377_6_pin9, or_51_out);
  xor xor_19 (xor_19_out, xor_20_out, or_50_out);
  xor xor_20 (xor_20_out, n74377_4_pin15, n74377_6_pin15);
  and and_72 (and_72_out, n74377_6_pin15, not_51_out);
  nand nand_1 (nand_1_out, in_1, in_2);
  nand nand_2 (nand_2_out, in_2, in_5);
  or or_47 (or_47_out, and_32_out, and_41_out);
  assign n74377_1_pin18 = and_41_out ? n74377_8_pin2 : 1'bz;  // Controlled_Buffer controlled_buffer_56
  assign n74377_1_pin18 = and_32_out ? n74377_8_pin5 : 1'bz;  // Controlled_Buffer controlled_buffer_57
  assign n74377_1_pin18 = and_33_out ? n74377_8_pin6 : 1'bz;  // Controlled_Buffer controlled_buffer_58
  _74377 #(.ShowInternalStructure("true")) u_74377_9 (
    .pin1(not_45_out), .pin2(n7485_1_pin10), .pin3(n74377_1_pin3), .pin4(n74377_1_pin4),
    .pin5(n7485_1_pin12), .pin6(n7485_1_pin13), .pin7(n74377_1_pin7), .pin8(n74377_1_pin8),
    .pin9(n7485_1_pin15), .pin19(n74377_9_pin19), .pin18(n74377_1_pin18), .pin17(n74377_1_pin17),
    .pin16(n74377_9_pin16), .pin15(n74377_9_pin15), .pin14(n74377_1_pin14), .pin13(n74377_1_pin13),
    .pin12(n74377_9_pin12), .pin11(n74377_1_pin11));
  and and_73 (and_73_out, not_49_out, xor_21_out);
  not not_49 (not_49_out, or_54_out);
  or or_48 (or_48_out, and_74_out, and_72_out);
  and and_74 (and_74_out, or_50_out, not_50_out);
  not not_50 (not_50_out, xor_20_out);
  not not_51 (not_51_out, n74377_4_pin15);
  nand nand_3 (nand_3_out, nand_1_out, nand_4_out);
  nand nand_4 (nand_4_out, nand_3_out, nand_2_out);
  _7485 #(.ShowInternalStructure("true")) u_7485_2 (
    .pin1(n7485_2_pin1), .pin2(n7485_1_pin7), .pin3(n7485_1_pin6), .pin4(n7485_1_pin5), .pin5(n74377_8_pin7),
    .pin6(n74377_8_pin4), .pin7(n74377_8_pin3), .pin15(n74377_9_pin12), .pin14(n7485_2_pin14),
    .pin13(n74377_9_pin15), .pin12(n74377_9_pin16), .pin11(n7485_2_pin11), .pin10(n74377_9_pin19),
    .pin9(n7485_2_pin9));
  or or_49 (or_49_out, and_73_out, and_75_out);
  and and_75 (and_75_out, or_54_out, xnor_5_out);
  xor xor_21 (xor_21_out, n74377_6_pin12, n74377_4_pin12);
  xor xor_22 (xor_22_out, xor_23_out, or_53_out);
  xor xor_23 (xor_23_out, n74377_4_pin16, n74377_6_pin16);
  LED led_4 (.in(nand_3_out));
  and and_76 (and_76_out, n74377_4_pin12, xor_24_out);
  xnor xnor_5 (xnor_5_out, n74377_6_pin12, n74377_4_pin12);
  or or_50 (or_50_out, and_77_out, and_78_out);
  and and_77 (and_77_out, or_53_out, not_52_out);
  not not_52 (not_52_out, xor_23_out);
  and and_78 (and_78_out, n74377_6_pin16, not_53_out);
  not not_53 (not_53_out, n74377_4_pin16);
  or or_51 (or_51_out, and_76_out, and_79_out);
  and and_79 (and_79_out, n74377_6_pin12, or_54_out);
  xor xor_24 (xor_24_out, n74377_6_pin12, or_54_out);
  xor xor_25 (xor_25_out, n74377_4_pin19, n74377_6_pin19);
  nor nor_1 (nor_1_out, \bit , nor_2_out);
  not not_54 (not_54_out, and_22_out);
  and and_80 (and_80_out, not_55_out, xor_27_out);
  not not_55 (not_55_out, or_56_out);
  xor xor_26 (xor_26_out, xor_25_out, 1'b0);
  and and_81 (and_81_out, 1'b0, not_57_out);
  and and_82 (and_82_out, n74377_6_pin19, not_56_out);
  not not_56 (not_56_out, n74377_4_pin19);
  or or_52 (or_52_out, and_80_out, and_83_out);
  and and_83 (and_83_out, or_56_out, xnor_6_out);
  xor xor_27 (xor_27_out, n74377_6_pin15, n74377_4_pin15);
  or or_53 (or_53_out, and_81_out, and_82_out);
  not not_57 (not_57_out, xor_25_out);
  nor nor_2 (nor_2_out, nor_1_out, \reg );
  _74377 #(.ShowInternalStructure("true")) u_74377_10 (
    .pin1(not_54_out), .pin2(n7485_2_pin9), .pin3(n74377_1_pin3), .pin4(n74377_1_pin4), .pin5(n7485_2_pin11),
    .pin6(n7485_2_pin14), .pin7(n74377_1_pin7), .pin8(n74377_1_pin8), .pin9(n7485_2_pin1),
    .pin19(n7485_1_pin9), .pin18(n74377_1_pin18), .pin17(n74377_1_pin17), .pin16(n7485_1_pin11),
    .pin15(n7485_1_pin14), .pin14(n74377_1_pin14), .pin13(n74377_1_pin13), .pin12(n7485_1_pin1),
    .pin11(n74377_1_pin11));
  and and_84 (and_84_out, n74377_4_pin15, xor_28_out);
  xnor xnor_6 (xnor_6_out, n74377_6_pin15, n74377_4_pin15);
  or or_54 (or_54_out, and_84_out, and_85_out);
  and and_85 (and_85_out, n74377_6_pin15, or_56_out);
  xor xor_28 (xor_28_out, n74377_6_pin15, or_56_out);
  and and_86 (and_86_out, not_58_out, xor_29_out);
  not not_58 (not_58_out, or_58_out);
  or or_55 (or_55_out, and_86_out, and_87_out);
  and and_87 (and_87_out, or_58_out, xnor_7_out);
  xor xor_29 (xor_29_out, n74377_6_pin16, n74377_4_pin16);
  not not_59 (not_59_out, in_11);
  nand s1 (s1_out, not_59_out, in_13);
  nand nand_5 (nand_5_out, nand_7_out, nand_6_out);
  and and_88 (and_88_out, not_60_out, not_62_out);
  not not_60 (not_60_out, n74377_1_pin3);
  and and_89 (and_89_out, n74377_4_pin16, xor_30_out);
  xnor xnor_7 (xnor_7_out, n74377_6_pin16, n74377_4_pin16);
  nand s3 (s3_out, s1_out, s4_out);
  nand nand_6 (nand_6_out, nand_5_out, not_61_out);
  not not_61 (not_61_out, and_34_out);
  nand nand_7 (nand_7_out, and_90_out, and_93_out);
  and and_90 (and_90_out, and_88_out, and_91_out);
  and and_91 (and_91_out, not_63_out, not_64_out);
  not not_62 (not_62_out, n74377_1_pin4);
  not not_63 (not_63_out, n74377_1_pin7);
  not not_64 (not_64_out, n74377_1_pin8);
  or or_56 (or_56_out, and_89_out, and_92_out);
  and and_92 (and_92_out, n74377_6_pin16, or_58_out);
  xor xor_30 (xor_30_out, n74377_6_pin16, or_58_out);
  and and_93 (and_93_out, and_94_out, and_96_out);
  and and_94 (and_94_out, not_65_out, not_66_out);
  not not_65 (not_65_out, n74377_1_pin13);
  not not_66 (not_66_out, n74377_1_pin14);
  not not_67 (not_67_out, n74377_1_pin17);
  and and_95 (and_95_out, not_68_out, xor_31_out);
  not not_68 (not_68_out, 1'b0);
  nand s2 (s2_out, in_13, in_11);
  nand s4 (s4_out, s3_out, s2_out);
  nand nand_8 (nand_8_out, nand_7_out, nand_9_out);
  and and_96 (and_96_out, not_67_out, not_69_out);
  not not_69 (not_69_out, n74377_1_pin18);
  or or_57 (or_57_out, and_95_out, and_97_out);
  and and_97 (and_97_out, 1'b0, xnor_8_out);
  xor xor_31 (xor_31_out, n74377_6_pin19, n74377_4_pin19);
  nand nand_9 (nand_9_out, nand_8_out, not_70_out);
  assign n74377_5_pin18 = and_42_out ? xor_26_out : 1'bz;  // Controlled_Buffer controlled_buffer_59
  assign n74377_5_pin17 = and_42_out ? xor_22_out : 1'bz;  // Controlled_Buffer controlled_buffer_60
  assign n74377_5_pin14 = and_42_out ? xor_19_out : 1'bz;  // Controlled_Buffer controlled_buffer_61
  assign n74377_5_pin13 = and_42_out ? xor_17_out : 1'bz;  // Controlled_Buffer controlled_buffer_62
  assign n74377_5_pin8 = and_42_out ? xor_12_out : 1'bz;  // Controlled_Buffer controlled_buffer_63
  assign n74377_5_pin7 = and_42_out ? xor_9_out : 1'bz;  // Controlled_Buffer controlled_buffer_64
  assign n74377_5_pin4 = and_42_out ? xor_6_out : 1'bz;  // Controlled_Buffer controlled_buffer_65
  assign n74377_5_pin3 = and_42_out ? xor_3_out : 1'bz;  // Controlled_Buffer controlled_buffer_66
  and and_98 (and_98_out, n74377_4_pin19, xor_32_out);
  xnor xnor_8 (xnor_8_out, n74377_6_pin19, n74377_4_pin19);
  not not_70 (not_70_out, and_35_out);
  or or_58 (or_58_out, and_98_out, and_99_out);
  and and_99 (and_99_out, n74377_6_pin19, 1'b0);
  xor xor_32 (xor_32_out, n74377_6_pin19, 1'b0);
  xor a1 (a1_out, A, B);
  and a3 (a3_out, C, a1_out);
  and a4 (a4_out, A, B);
  xor a2 (a2_out, a1_out, C);
  or a5 (a5_out, a3_out, a4_out);
  // also tied to GND on the sheet: {n74377_8_pin1, n7485_1_pin2, n7485_1_pin4, n74377_8_pin8}
  // also tied to VCC on the sheet: n7485_1_pin3

  // Notes on the sheet:
  //   2
  //   in / write register
  //   1
  //   out / read register
  //   + / -
  //   sum data bus enable
  //   in enable
  //   in enable
  //   out enable
  //   manual reset code
  //   out enable
  //   in enable
  //   out enable
  //   register sum 2 enable
  //   register sum 1 enable
  //   AX
  //   AL
  //   AH
  //   in
  //   out
  //   sum data out
  //   contents of rom_1 (hex, n*v repeats v):
  //   0 45 a 6*0 78
  //   2 (in registers)
  //   1 (out)
  //   EAX
  //   contents of rom_2 (hex, n*v repeats v):
  //   0 5 3 32 80 41 7 45 16 8
  //   out < > =
  //   in comparator
  //   A
  //   CM
  //   OUT PIN 1 / 2
  //   s1
  //   s2
  //   B
  //   CM
  //   ~Q
  //   CLK
  //   Q
  //   S
  //   Cout
endmodule
